# Fritzing sketch arm circuit (saved by Fritzing 1.0.3b)
breadboards: 1

parts:
  Part1 = Arduino Mega 2560 (Rev3)
  Part2 = 16-Channel 12-bit PWM Servo Driver - I2C [part_number=815]
  Part3 = Bluetooth HC-05 Macho
  IC1 = L293D [package=THT]
  VCC1 = 4 x AAA Battery Mount [internal_resistance=0.1Ω]
  VCC2 = Battery block 9V [internal_resistance=0.1Ω]
  M1 = DC Motor [voltage_(max)=6V voltage_(min)=3V]
  M2 = DC Motor [voltage_(max)=6V voltage_(min)=3V]
  J1 = Basic Servo
  J2 = Basic Servo
  J3 = Basic Servo
  J4 = Basic Servo

nets:
  N1: Part1.D21/SCL, Part1.SCL, Part2.SCL
  N2: Part1.D20/SDA, Part1.SDA, Part2.SDA
  N3: Part1.D9_PWM, IC1.Enable_2
  N4: Part1.D8_PWM, IC1.In_3
  VCC: Part1.5V, Part2.VCC, Part3.VCC, IC1.+Vmotor
  GND: Part1.GND, Part2.OE, Part3.GND, IC1.0V, VCC2.-
  N5: Part1.D0_RX0, Part3.RXD
  N6: Part1.D1_TX0, Part3.TXD
  N7: Part1.D3_PWM, IC1.Enable_1
  N8: Part1.D4_PWM, IC1.In_2
  N9: Part1.D5_PWM, IC1.In_1
  N10: Part1.D7_PWM, IC1.In_4
  VCC_2: Part2.5.0V, J1.vcc, J2.vcc, J3.vcc, J4.vcc
  N11: Part2.PWRIN, VCC1.+
  GND_2: Part2.GND, VCC1.-, J1.gnd, J2.gnd, J3.gnd, J4.gnd
  N12: Part2.PWM3, J4.pulse
  N13: Part2.PWM2, J3.pulse
  N14: Part2.PWM1, J2.pulse
  N15: Part2.PWM0, J1.pulse
  N16: IC1.Out_1_(_Controlled_by_Enable_1_), M1.pin_2
  N17: IC1.Out_2_(_Controlled_by_Enable_1_), M1.pin_1
  N18: IC1.Out_3_(_Controlled_by_Enable_2_), M2.pin_2
  N19: IC1.Out_4_(_Controlled_by_Enable_2_), M2.pin_1
  N20: IC1.+V, VCC2.+

custom parts:
  16-Channel 12-bit PWM Servo Driver - I2C: You want to make a cool robot, maybe a hexapod walker, or maybe just a piece of art with a lot of moving parts. Or maybe you want to drive a lot of LEDs with precise PWM output. Using only two pins, control 16 free-running PWM outputs! You can even chain up 62 breakouts to control up to 992 PWM outputs.
