# Fritzing sketch glove circuit (saved by Fritzing 1.0.3b)
breadboards: 1

parts:
  Part2 = Arduino Nano (Rev3.0)
  VCC1 = Battery block 9V [internal_resistance=0.1Ω]
  Part3 = Bluetooth HC-05 Macho
  Part4 = InvenSense MPU6050
  R1 = Basic Flex Resistor
  R2 = Resistor [tolerance=±5% resistance=220 package="2010 [SMD]"]

nets:
  N1: Part2.D1/TX, Part3.TXD
  N2: Part2.D0/RX, Part3.RXD
  GND: Part2.GND, VCC1.-, Part3.GND, Part4.GND, R1.Pin_2
  N3: Part2.D2, Part4.INT
  N4: Part2.VIN, VCC1.+
  VCC: Part2.5V, Part3.VCC, Part4.VCC, R2.Pin_1
  N5: Part2.A5, Part4.SCL
  N6: Part2.A4, Part4.SDA
  N7: Part2.A0, R1.pin_1, R2.Pin_0
